# Fritzing sketch CapstoneV1 (saved by Fritzing 0.9.4)
breadboards: 3

parts:
  Argon1 = Particle Argon
  Part1 = MQ-131 breakout
  Part2 = Adafruit MicroSD card breakout board [part_number="Adafruit #254"]
  OLED_I2C1 = OLED 128x64 I2C Monochrome Display
  M1 = BMP280
  S1 = Pushbutton [package="[THT]"]
  IC1 = DIP - 8 pins [part_number=LM741 package="DIP (Dual Inline) [THT]"]
  C1 = Capacitor [package=cap-pth-small2]
  C2 = Capacitor [package=cap-pth-small2]
  C3 = Capacitor [package=cap-pth-small2]
  R1 = Resistor [tolerance=±5% resistance=220 package=THT]
  R2 = Resistor [tolerance=±5% resistance=47k package=THT]
  R3 = Resistor [tolerance=±5% resistance=47k package=THT]
  R4 = Resistor [tolerance=±5% resistance=1k package=THT]
  IC2 = DIP - 8 pins [part_number=LM741 package="DIP (Dual Inline) [THT]"]
  C4 = Capacitor [package=cap-pth-small2]
  C5 = Capacitor [package=cap-pth-small2]
  C6 = Capacitor [package=cap-pth-small2]
  R5 = Resistor [tolerance=±5% resistance=220 package=THT]
  R6 = Resistor [tolerance=±5% resistance=47k package=THT]
  R7 = Resistor [tolerance=±5% resistance=47k package=THT]
  R8 = Resistor [tolerance=±5% resistance=1k package=THT]
  WS2812B1 = WS2812B [package="DIP (Dual Inline) [THT]"]
  DFRobot_DFPlayer_Mini1 = DFRobot DFPlayer Mini [part_number=DFR0299]

nets (from the breadboard view):
  VCC: Argon1.3.3V, Part1.VCC, DFRobot_DFPlayer_Mini1.VCC
  GND: Argon1.GND, Part1.GND, Part2.GND, OLED_I2C1.GND, S1.Pin_1, S1.Pin_2, IC1.pin4, C1.2, R3.Pin_1, IC2.pin4, R7.Pin_1, WS2812B1.GND, DFRobot_DFPlayer_Mini1.GND-1, DFRobot_DFPlayer_Mini1.GND-2
  N1: Argon1.A1, Part1.AO
  N2: Argon1.A3, Part2.CS
  N3: Argon1.SCK, Part2.CLK
  N4: Argon1.MO, Part2.DI
  N5: Argon1.MI, Part2.DO
  N6: Argon1.SDA, OLED_I2C1.SDA, M1.SDA
  N7: Argon1.SCL, OLED_I2C1.SCK, M1.SCL
  N8: Argon1.D4, WS2812B1.DI
  N9: Argon1.D8, S1.Pin_3, S1.Pin_4
  VCC_2: Argon1.VUSB, Part2.VCC, OLED_I2C1.VDD, M1.VIN, WS2812B1.5V
  N10: M1.GND, C5.2
  N11: IC1.pin1, R1.Pin_1
  N12: IC1.pin2, R4.Pin_1
  N13: IC1.pin3, R2.Pin_0, R3.Pin_0
  N14: IC1.pin6, C3.1, R1.Pin_0
  N15: IC1.pin7, C1.1, R2.Pin_1, IC2.pin7, C5.1, R6.Pin_1
  N16: C2.1, DFRobot_DFPlayer_Mini1.DAC_L
  N17: C2.2, R4.Pin_0
  N18: IC2.pin1, R5.Pin_1
  N19: IC2.pin2, R8.Pin_1
  N20: IC2.pin3, R6.Pin_0, R7.Pin_0
  N21: IC2.pin6, C4.1, R5.Pin_0
  N22: C6.1, DFRobot_DFPlayer_Mini1.DAC_R
  N23: C6.2, R8.Pin_0

custom parts:
  Particle Argon: The Argon is a powerful Wi-Fi enabled development board that can act as either a standalone Wi-Fi endpoint or Wi-Fi enabled gateway for Particle Mesh networks. It is based on the Nordic nRF52840 and has built-in battery charging circuitry so it’s easy to connect a Li-Po and deploy your local network in minutes. The Argon is great for connecting existing projects to the Particle Device Cloud or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
  MQ-131 breakout: SKU: 101282
  Adafruit MicroSD card breakout board: Not just a simple breakout board, this microSD adapter goes the extra mile - designed for ease of use. Onboard 5v->3v regulator provides 150mA for power-hungry cards 3v level shifting means you can use this with ease on either 3v or 5v systems Uses a proper level shifting chip, not resistors: less problems, and faster read/write access Use 3 or 4 digital pins to read and write 2Gb+ of storage!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
  BMP280: Temperature Humidity Barometric presure Sensor, I2C
  Pushbutton: A generic pushbutton.
  DIP - 8 pins: A DIP stand-in part for whatever IC you want. With 8 pins on a 300 mil dual inline package (DIP) footprint.
  WS2812B: Adafruit NeoPixel Breakout
