# Fritzing sketch CapstoneV2 (saved by Fritzing 0.9.4)
breadboards: 3

parts:
  Breadboard4 = Breadboard Split Power
  Breadboard5 = Breadboard Split Power
  Argon1 = Particle Argon
  WS2812B1 = WS2812B [package="DIP (Dual Inline) [THT]"]
  WS2812B2 = WS2812B [package="DIP (Dual Inline) [THT]"]
  M1 = BMP280
  Part1 = Adafruit MicroSD card breakout board [part_number="Adafruit #254"]
  DFRobot_DFPlayer_Mini1 = DFRobot DFPlayer Mini [part_number=DFR0299]
  S2 = Pushbutton [package="[THT]"]
  R1 = PHOTOCELL [package=photocell-kit]
  Part2 = MQ-131 breakout
  IC1 = IC, DIP package, 8 pins [chip_label=2134]
  IC2 = IC, DIP package, 8 pins [chip_label=2134]
  C1 = Capacitor [package=cap-pth-small2]
  R2 = Trimmer Potentiometer [maximum_resistance=5kΩ package=THT]
  R3 = Trimmer Potentiometer [maximum_resistance=5kΩ package=THT]
  R4 = Trimmer Potentiometer [maximum_resistance=2kΩ package=THT]
  R5 = Trimmer Potentiometer [maximum_resistance=2kΩ package=THT]
  R6 = Trimmer Potentiometer [maximum_resistance=2kΩ package=THT]
  R7 = Trimmer Potentiometer [maximum_resistance=2kΩ package=THT]
  C2 = Capacitor [package=cap-pth-small2]
  C3 = Capacitor [package=cap-pth-small2]
  C4 = Capacitor [package=cap-pth-small2]
  WS2812B3 = WS2812B [package="DIP (Dual Inline) [THT]"]
  Part3 = MQ-131 breakout [part_number=9]
  U1 = LIPO-1000mAh [package=lipo-1000]  # not connected

nets:
  GND: Breadboard4.pin3Z, Breadboard4.pin20Z, Breadboard4.pin29Z, Breadboard5.pin3Z, Breadboard5.pin11Z, Argon1.GND, WS2812B1.GND, WS2812B2.GND, M1.GND, Part1.GND, DFRobot_DFPlayer_Mini1.GND-1, DFRobot_DFPlayer_Mini1.GND-2, Part2.GND, IC1.pin3, IC1.pin4, C2.1, WS2812B3.GND, Part3.GND
  5V: Breadboard4.pin4Y, Breadboard4.pin15Y, Breadboard4.pin17Y, Breadboard4.pin21Y, Breadboard4.pin29Y, Breadboard5.pin3Y, Breadboard5.pin12Y, Breadboard5.pin15Y, Breadboard5.pin17Y, Argon1.VUSB, WS2812B1.5V, WS2812B2.5V, M1.VIN, Part1.+3V3, DFRobot_DFPlayer_Mini1.VCC, S2.Pin_1, S2.Pin_2, Part2.VCC, IC1.pin8, IC2.pin8, WS2812B3.5V, Part3.VCC
  N1: Argon1.A0, WS2812B1.DI
  N2: Argon1.A3, Part2.AO
  N3: Argon1.A5, Part1.CS
  N4: Argon1.SCK, Part1.CLK
  N5: Argon1.MO, Part1.DI
  N6: Argon1.RX, DFRobot_DFPlayer_Mini1.TX
  N7: Argon1.TX, DFRobot_DFPlayer_Mini1.RX
  N8: Argon1.SDA, M1.SDA, Part3.AO
  N9: Argon1.SCL, M1.SCL, Part3.DO
  N10: Argon1.D2, S2.Pin_3, S2.Pin_4
  N11: Argon1.D3, R1.P$2
  N12: WS2812B1.DO, WS2812B2.DI
  N13: WS2812B2.DO, WS2812B3.DI
  N14: DFRobot_DFPlayer_Mini1.DAC_R, R5.leg1
  N15: DFRobot_DFPlayer_Mini1.DAC_L, R6.leg1
  N16: R1.P$1, IC2.pin3, IC2.pin4, C3.1
  N17: IC1.pin1, IC1.pin2, C1.1, C1.2, R2.wiper, R2.leg2, R4.leg1, C2.2
  N18: IC2.pin1, IC2.pin2, R3.wiper, R3.leg2, R7.leg1, C3.2, C4.1, C4.2
  N19: R4.wiper, R5.wiper
  N20: R6.wiper, R7.wiper

notes:
  Transducers signal wires go here and to ground

custom parts:
  Breadboard Split Power: A custom 6 pin per group power supply strip where the top row (ground) is all bussed together and the bottom row (+V) is split in two groups of 12 pins. This version is modified to be a loadable part and was rescaled to be on the standard 1px = 1thou grid with the size set in inches
  Particle Argon: The Argon is a powerful Wi-Fi enabled development board that can act as either a standalone Wi-Fi endpoint or Wi-Fi enabled gateway for Particle Mesh networks. It is based on the Nordic nRF52840 and has built-in battery charging circuitry so it’s easy to connect a Li-Po and deploy your local network in minutes. The Argon is great for connecting existing projects to the Particle Device Cloud or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
  WS2812B: Adafruit NeoPixel Breakout
  BMP280: Temperature Humidity Barometric presure Sensor, I2C
  Adafruit MicroSD card breakout board: Not just a simple breakout board, this microSD adapter goes the extra mile - designed for ease of use. Onboard 5v->3v regulator provides 150mA for power-hungry cards 3v level shifting means you can use this with ease on either 3v or 5v systems Uses a proper level shifting chip, not resistors: less problems, and faster read/write access Use 3 or 4 digital pins to read and write 2Gb+ of storage!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
  Pushbutton: A generic pushbutton.
  MQ-131 breakout: SKU: 101282
