# Fritzing sketch high_gain_opamp (saved by Fritzing 0.9.4)
breadboards: 1

parts:
  U1 = OP27 - Low Noise, Precision Op Amp [part_number=OP27]
  C1 = Capacitor [package=cap-pth-small2]
  R1 = Resistor [tolerance=±5% resistance=47k package=THT]
  C2 = Capacitor [package=cap-pth-small2]
  R2 = Resistor [tolerance=±5% resistance=47k package=THT]
  R3 = Resistor [tolerance=±5% resistance=100k package=THT]
  R4 = Resistor [tolerance=±5% resistance=1k package=THT]
  C3 = Capacitor [package=cap-pth-small2]

nets:
  N1: U1.-IN, R3.Pin_0, R4.Pin_0
  N2: U1.+IN, R1.Pin_0, R2.Pin_1
  N3: U1.-V, R1.Pin_1, C2.2
  N4: U1.OUT, C1.1, R3.Pin_1
  N5: U1.V+, C2.1, R2.Pin_0
  N6: R4.Pin_1, C3.2

notes:
  <-- signal output
  <-- +Vcc
  signal input -->
  bottom row capacitors = .01uf
  top row capacitors = 10um
  100K ohm way too high. lowered to 10k and maybe using a potentiometer
